// Logisim project ALU.circ as structural Verilog: 1 circuit, main circuit ALU
module ALU (
  input  [31:0] in_1,
  input  [31:0] in_2,
  output [31:0] out_3
);

  wire comparator_1_lt, comparator_2_lt;
  wire [31:0] add, \and , divuHi, divuLo, muluHi, muluLo, \nor , \or , slt, stlu, sub, \xor ;

  Adder #(.width(32)) adder_1 (.a(in_1), .b(in_2), .out(add));  // open: cin, cout
  Subtractor #(.width(32)) subtractor_1 (.a(in_1), .b(in_2), .out(sub));  // open: bin, bout
  Comparator #(.width(32)) comparator_1 (.a(in_1), .b(in_2), .lt(comparator_1_lt));  // open: gt, eq
  assign slt = {{31{1'b0}}, comparator_1_lt};  // Bit_Extender bit_extender_1
  Comparator #(.width(32), .mode("unsigned")) comparator_2 (.a(in_1), .b(in_2), .lt(comparator_2_lt));  // open: gt, eq
  assign stlu = {{31{1'b0}}, comparator_2_lt};  // Bit_Extender bit_extender_2
  Multiplier #(.width(32)) multiplier_1 (.a(in_1), .b(in_2), .out(muluLo), .cout(muluHi));  // open: cin
  Divider #(.width(32)) divider_1 (.a(in_1), .b(in_2), .out(divuLo), .rem(divuHi));  // open: upper
  Multiplexer #(.select(4), .width(32)) multiplexer_1 (.out(out_3));  // open: in0, in1, in2, in3, in4, in5, in6, in7, in8, in9, in10, in11, in12, in13, in14, in15, sel, en
  assign \and  = in_1 & in_2;  // AND_Gate and_1, 32 bits wide
  assign \or  = in_1 | in_2;  // OR_Gate or_1, 32 bits wide
  assign \xor  = in_1 ^ in_2;  // XOR_Gate xor_1, 32 bits wide
  assign \nor  = ~(in_1 | in_2);  // NOR_Gate nor_1, 32 bits wide

  // Other names for the same wires on the sheet: A[31:0] = in_1; B[31:0] = in_2; F[31:0] = out_3

  // Notes on the sheet:
  //   Inputs
  //   Arithmetics
  //   ALU
  //   Logics
  //   Outputs
endmodule
