// Logisim project Data Path.circ as structural Verilog: 1 circuit, main circuit Data Path
module Data_Path (
  input  in_1
);

  wire instruction_decoder_1_out_4, instruction_decoder_1_out_19, instruction_decoder_1_out_21;
  wire [1:0] BC_selector;
  wire [2:0] Flag_Condition, instruction_decoder_1_out_6;
  wire [3:0] instruction_decoder_1_out_3;
  wire [4:0] instruction_decoder_1_out_10, instruction_decoder_1_selector_a, instruction_decoder_1_selector_b;
  wire [15:0] offset;
  wire [25:0] Dest;
  wire [31:0] alu_1_out_4, alu_1_out_5, alu_input_1_out_5, hi_lo_1_out_5, hi_lo_1_out_6,
       instruction_memory_1_out_5, program_counter_1_p1, program_counter_1_p3, register_file_input_1_out_9,
       Rs, Rt, Rt_t;

  Instruction_Memory instruction_memory_1 (.out_5(instruction_memory_1_out_5), .clk(in_1));  // open: in_1, en, reset
  Instruction_Decoder instruction_decoder_1 (
    .in_1(instruction_memory_1_out_5), .out_3(instruction_decoder_1_out_3),
    .out_4(instruction_decoder_1_out_4), .out_19(instruction_decoder_1_out_19),
    .BC_jump_Selector(BC_selector), .Flag_Condition(Flag_Condition), .out_10(instruction_decoder_1_out_10),
    .out_6(instruction_decoder_1_out_6), .out_21(instruction_decoder_1_out_21),
    .Selector_A(instruction_decoder_1_selector_a), .Selector_B(instruction_decoder_1_selector_b),
    .out_14(offset), .out_17(Dest));  // open: in_2, out_11, out_13, out_9, Stop_program, out_23, save_word, keyboard, pop, push, out_7
  // Program_Counter program_counter_1: pin names not known; wires that end beside it: program_counter_1_p1, in_1, program_counter_1_p3
  Register_File_Input register_file_input_1 (
    .RF_Selector(instruction_decoder_1_out_6), .in_2(alu_1_out_4), .in_3(in_1), .in_5(hi_lo_1_out_5),
    .in_6(hi_lo_1_out_6), .out_9(register_file_input_1_out_9));  // open: in_4, Keyboard, in_8
  // Register_File register_file_1: pin names not known; wires that end beside it: register_file_input_1_out_9, instruction_decoder_1_out_10, in_1, instruction_decoder_1_selector_a, instruction_decoder_1_selector_b, Rs, Rt
  Branch_Control branch_control_1 (
    .in_1(Rs), .in_2(Rt_t), .in_3(program_counter_1_p3), .in_4(Dest), .in_5(offset),
    .Fag_Condition(Flag_Condition), .Jump_Selector(BC_selector), .out_8(program_counter_1_p1));
  ALU_Input alu_input_1 (
    .in_1(Rt), .constant(instruction_decoder_1_out_19), .in_3(offset),
    .Is_Inmediate(instruction_decoder_1_out_21), .out_5(alu_input_1_out_5));
  ALU alu_1 (
    .in_1(Rs), .in_2(alu_input_1_out_5), .in_3(instruction_decoder_1_out_3), .out_4(alu_1_out_4),
    .out_5(alu_1_out_5));
  Hi_Lo hi_lo_1 (
    .in_1(alu_1_out_4), .in_2(alu_1_out_5), .in_3(instruction_decoder_1_out_4), .in_4(in_1),
    .out_5(hi_lo_1_out_5), .out_6(hi_lo_1_out_6));

  // Other names for the same wires on the sheet: clk = in_1
endmodule
