// Logisim project Register File.circ as structural Verilog: 1 circuit, main circuit Register File
module Register_File (
  input  in_1,
  input  [4:0] in_2,
  input  [31:0] in_3,
  input  in_4,
  input  in_5,
  input  [4:0] in_6,
  input  [4:0] in_7,
  output [31:0] out_8,
  output [31:0] out_9
);

  wire L0, L1, L2, L3, L4, L5, L6, L7, L8, L9, L10, L11, L12, L13, L14, L15, L16, L17, L18, L19, L20, L21,
       L22, L23, L24, L25, L26, L27, L28, L29, L30, L31;
  wire [31:0] Q0, Q1, Q2, Q3, Q4, Q5, Q6, Q7, Q8, Q9, Q10, Q11, Q12, Q13, Q14, Q15, Q16, Q17, Q18, Q19, Q20,
       Q21, Q22, Q23, Q24, Q25, Q26, Q27, Q28, Q29, Q30, Q31;

  Register #(.width(32)) register_1 (.D(in_3), .en(in_5), .Q(Q0), .clk(in_1), .clr(1'b0));
  Register #(.width(32)) register_2 (.D(in_3), .en(in_5), .Q(Q8), .clk(in_1), .clr(L8));
  Register #(.width(32)) register_3 (.D(in_3), .en(in_5), .Q(Q16), .clk(in_1), .clr(L16));
  Register #(.width(32)) register_4 (.D(in_3), .en(in_5), .Q(Q24), .clk(in_1), .clr(L24));
  Register #(.width(32)) register_5 (.D(in_3), .en(in_5), .Q(Q1), .clk(in_1), .clr(L1));
  Register #(.width(32)) register_6 (.D(in_3), .en(in_5), .Q(Q9), .clk(in_1), .clr(L9));
  Register #(.width(32)) register_7 (.D(in_3), .en(in_5), .Q(Q17), .clk(in_1), .clr(L17));
  Register #(.width(32)) register_8 (.D(in_3), .en(in_5), .Q(Q25), .clk(in_1), .clr(L25));
  Register #(.width(32)) register_9 (.D(in_3), .en(in_5), .Q(Q2), .clk(in_1), .clr(L2));
  Register #(.width(32)) register_10 (.D(in_3), .en(in_5), .Q(Q10), .clk(in_1), .clr(L10));
  Register #(.width(32)) register_11 (.D(in_3), .en(in_5), .Q(Q18), .clk(in_1), .clr(L18));
  Register #(.width(32)) register_12 (.D(in_3), .en(in_5), .Q(Q26), .clk(in_1), .clr(L26));
  Decoder #(.select(5), .disabled(0)) decoder_1 (
    .out0(L0), .out1(L1), .out2(L2), .out3(L3), .out4(L4), .out5(L5), .out6(L6), .out7(L7), .out8(L8),
    .out9(L9), .out10(L10), .out11(L11), .out12(L12), .out13(L13), .out14(L14), .out15(L15), .out16(L16),
    .out17(L17), .out18(L18), .out19(L19), .out20(L20), .out21(L21), .out22(L22), .out23(L23), .out24(L24),
    .out25(L25), .out26(L26), .out27(L27), .out28(L28), .out29(L29), .out30(L30), .out31(L31), .sel(in_2),
    .en(in_4));
  Register #(.width(32)) register_13 (.D(in_3), .en(in_5), .Q(Q3), .clk(in_1), .clr(L3));
  Register #(.width(32)) register_14 (.D(in_3), .en(in_5), .Q(Q11), .clk(in_1), .clr(L11));
  Register #(.width(32)) register_15 (.D(in_3), .en(in_5), .Q(Q19), .clk(in_1), .clr(L19));
  Register #(.width(32)) register_16 (.D(in_3), .en(in_5), .Q(Q27), .clk(in_1), .clr(L27));
  Register #(.width(32)) register_17 (.D(in_3), .en(in_5), .Q(Q4), .clk(in_1), .clr(L4));
  Register #(.width(32)) register_18 (.D(in_3), .en(in_5), .Q(Q12), .clk(in_1), .clr(L12));
  Register #(.width(32)) register_19 (.D(in_3), .en(in_5), .Q(Q20), .clk(in_1), .clr(L20));
  Register #(.width(32)) register_20 (.D(in_3), .en(in_5), .Q(Q28), .clk(in_1), .clr(L28));
  Multiplexer #(.select(5), .width(32), .enable("false")) multiplexer_1 (
    .in0(Q0), .in1(Q1), .in2(Q2), .in3(Q3), .in4(Q4), .in5(Q5), .in6(Q6), .in7(Q7), .in8(Q8), .in9(Q9),
    .in10(Q10), .in11(Q11), .in12(Q12), .in13(Q13), .in14(Q14), .in15(Q15), .in16(Q16), .in17(Q17),
    .in18(Q18), .in19(Q19), .in20(Q20), .in21(Q21), .in22(Q22), .in23(Q23), .in24(Q24), .in25(Q25),
    .in26(Q26), .in27(Q27), .in28(Q28), .in29(Q29), .in30(Q30), .in31(Q31), .out(out_8), .sel(in_6));
  Register #(.width(32)) register_21 (.D(in_3), .en(in_5), .Q(Q5), .clk(in_1), .clr(L5));
  Register #(.width(32)) register_22 (.D(in_3), .en(in_5), .Q(Q13), .clk(in_1), .clr(L13));
  Register #(.width(32)) register_23 (.D(in_3), .en(in_5), .Q(Q21), .clk(in_1), .clr(L21));
  Register #(.width(32)) register_24 (.D(in_3), .en(in_5), .Q(Q29), .clk(in_1), .clr(L29));
  Register #(.width(32)) register_25 (.D(in_3), .en(in_5), .Q(Q6), .clk(in_1), .clr(L6));
  Register #(.width(32)) register_26 (.D(in_3), .en(in_5), .Q(Q14), .clk(in_1), .clr(L14));
  Register #(.width(32)) register_27 (.D(in_3), .en(in_5), .Q(Q22), .clk(in_1), .clr(L22));
  Register #(.width(32)) register_28 (.D(in_3), .en(in_5), .Q(Q30), .clk(in_1), .clr(L30));
  Multiplexer #(.select(5), .width(32), .enable("false")) multiplexer_2 (
    .in0(Q0), .in1(Q1), .in2(Q2), .in3(Q3), .in4(Q4), .in5(Q5), .in6(Q6), .in7(Q7), .in8(Q8), .in9(Q9),
    .in10(Q10), .in11(Q11), .in12(Q12), .in13(Q13), .in14(Q14), .in15(Q15), .in16(Q16), .in17(Q17),
    .in18(Q18), .in19(Q19), .in20(Q20), .in21(Q21), .in22(Q22), .in23(Q23), .in24(Q24), .in25(Q25),
    .in26(Q26), .in27(Q27), .in28(Q28), .in29(Q29), .in30(Q30), .in31(Q31), .out(out_9), .sel(in_7));
  Register #(.width(32)) register_29 (.D(in_3), .en(in_5), .Q(Q7), .clk(in_1), .clr(L7));
  Register #(.width(32)) register_30 (.D(in_3), .en(in_5), .Q(Q15), .clk(in_1), .clr(L15));
  Register #(.width(32)) register_31 (.D(in_3), .en(in_5), .Q(Q23), .clk(in_1), .clr(L23));
  Register #(.width(32)) register_32 (.D(in_3), .en(in_5), .Q(Q31), .clk(in_1), .clr(L31));

  // Other names for the same wires on the sheet: A[31:0] = out_8; B[31:0] = out_9; clk = in_1; DA[4:0] = in_2;
  //   DI[31:0] = in_3; Rst = in_5; RW = in_4; SA[4:0] = in_6; SB[4:0] = in_7

  // Notes on the sheet:
  //   Inputs
  //   R0
  //   R8
  //   R16
  //   R24
  //   R1
  //   R9
  //   R17
  //   R25
  //   R2
  //   R10
  //   R18
  //   R26
  //   R3
  //   R11
  //   R19
  //   R27
  //   REGISTER FILE
  //   R4
  //   R12
  //   R20
  //   R28
  //   R5
  //   R13
  //   R21
  //   R29
  //   R6
  //   R14
  //   R22
  //   R30
  //   R7
  //   R15
  //   R23
  //   R31
  //   Outputs
endmodule
